# Fritzing sketch MicronetToNMEA_DC_Power (saved by Fritzing 0.9.3b)

parts:
  Teensy_3_5 = Teensy 3.6 (Basic)
  DC-DC_Converter = DC-DC CONVERTER [part_number=80633 package=dc-dc_converter]
  Lead_battery = 12 battery [package=battery]

nets:
  GND: Teensy_3_5.GND, Teensy_3_5.GND1, DC-DC_Converter.OUT-
  N1: Teensy_3_5.Vin, DC-DC_Converter.OUT+
  N2: DC-DC_Converter.IN-, Lead_battery.-
  N3: DC-DC_Converter.IN+, Lead_battery.+

notes:
  +3.3V
  +5V
  +12V

custom parts:
  Teensy 3.6 (Basic): The Teensy is a complete USB-based microcontoller development system, in a very small footprint, capable of implementing many types of projects. All programming is done via the USB port. No special programmer is needed, only a standard micro-USB cable and a PC or Macintosh with a USB port.
  DC-DC CONVERTER: WYHP 5A constant current/voltage manufactured by Shenzhen Weiyapuhua Technology Co., Ltd
  12 battery: 12V lead acid type battery, like the Husqvarna YTH2448 12V 35AH battery. This is the mini version 1/4 the size of the actual battery to be closer to typical breadboard parts (around 2in wide rathher than 7in). The pads in pcb are sized to accomidate up to 14ga wire (as these batterys will deliver high currents.)
