# Fritzing sketch MicronetToNMEA_GNSS (saved by Fritzing 0.9.3b)

parts:
  Teensy1 = Teensy 3.6 (Basic)
  UBLOX_M8N = SUP500F [package=sup500f]

nets:
  GND: Teensy1.GND, Teensy1.GND1, UBLOX_M8N.GND
  N1: Teensy1.D0, UBLOX_M8N.TX-O
  N2: Teensy1.D1, UBLOX_M8N.RX-I
  VIN: Teensy1.Vin, UBLOX_M8N.VCC

notes:
  VCC
  GND
  TX
  RX

custom parts:
  Teensy 3.6 (Basic): The Teensy is a complete USB-based microcontoller development system, in a very small footprint, capable of implementing many types of projects. All programming is done via the USB port. No special programmer is needed, only a standard micro-USB cable and a PC or Macintosh with a USB port.
