# Fritzing sketch MicronetToNMEA_HC06 (saved by Fritzing 0.9.3b)

parts:
  Teensy1 = Teensy 3.6 (Basic)
  BT1 = Bluetooth HC-06d [package=THT]

nets:
  N1: Teensy1.A6/D20, BT1.RXD
  N2: Teensy1.A7/D21, BT1.TXD
  N3: Teensy1.AGND, BT1.GND
  VIN: Teensy1.Vin, BT1.VCC

notes:
  TX
  RX

custom parts:
  Teensy 3.6 (Basic): The Teensy is a complete USB-based microcontoller development system, in a very small footprint, capable of implementing many types of projects. All programming is done via the USB port. No special programmer is needed, only a standard micro-USB cable and a PC or Macintosh with a USB port.
  Bluetooth HC-06d: Bluetooth HC-06 - face down, pins down 16.5mm x 37.5mm PCB
