# Fritzing sketch MicronetToNMEA_LSM303 (saved by Fritzing 0.9.3b)

parts:
  Teensy1 = Teensy 3.6 (Basic)
  Composant1 = Adafruit LSM303DLHC Triple-axis Accelerometer+Magnetometer (Compass) [part_number="Adafruit #1120"]

nets:
  GND: Teensy1.GND, Teensy1.GND1, Composant1.GND
  3V3: Teensy1.3V3, Teensy1.3V3_1, Composant1.3.3V
  N1: Teensy1.D37, Composant1.SCL
  N2: Teensy1.D38, Composant1.SDA

custom parts:
  Teensy 3.6 (Basic): The Teensy is a complete USB-based microcontoller development system, in a very small footprint, capable of implementing many types of projects. All programming is done via the USB port. No special programmer is needed, only a standard micro-USB cable and a PC or Macintosh with a USB port.
  Adafruit LSM303DLHC Triple-axis Accelerometer+Magnetometer (Compass): He told you "Go West, young maker!" - but you don't know which way is West! Ah, if only you had this triple-axis accelerometer/magnetometer compass module. Inside are two sensors, one is a classic 3-axis accelerometer, which can tell you which direction is down towards the Earth (by measuring gravity). The other is a magnetometer that can sense where the strongest magnetic force is coming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
